# Fritzing sketch PWM_Pote_LED (saved by Fritzing 0.8.3b)
breadboards: 1

parts:
  Part2 = Arduino Uno (Rev3)
  R1 = Rotary Potentiometer (Small)
  LED1 = LED - 5mm [color="Red (633nm)" package="5 mm [THT]"]  # not connected
  R2 = Resistor [tolerance=±5% resistance=220 package=THT]

nets:
  N1: Part2.A3, R1.wiper
  N2: Part2.GND, R1.leg2
  N3: Part2.D9_PWM, R2.Pin_1
  N4: Part2.5V, R1.leg1
